// Logisim project maybeProject.circ as structural Verilog
// 12
module main (
  input  [31:0] in_1,
  input  [31:0] in_2,
  input  [31:0] in_3,
  input  [31:0] in_4,
  input  [31:0] in_5,
  input  [31:0] in_6,
  input  [31:0] in_7,
  input  [31:0] in_8,
  input  [31:0] in_9,
  input  [31:0] in_10,
  input  [31:0] in_11,
  input  [31:0] in_12,
  input  [31:0] in_13,
  input  [31:0] in_14,
  input  [31:0] in_15,
  input  [31:0] in_16,
  input  [31:0] in_17,
  input  [31:0] in_18,
  input  [31:0] in_19,
  input  [31:0] in_20,
  input  [31:0] in_21,
  input  [31:0] in_22,
  input  [31:0] in_23,
  input  [31:0] in_24,
  input  [31:0] in_25,
  input  [31:0] in_26,
  input  [31:0] in_27,
  input  [31:0] in_28,
  input  [31:0] in_29,
  input  [31:0] in_30,
  input  [31:0] in_31,
  input  [31:0] in_32
);

  wire button_1_out, clock_1_out;
  wire [31:0] _1, _2, _3, _4, _5, _6, _9, _10, _11, _12, _13, _14, _15, _16, _17, _18, _19, _20, _21, _22,
       _23, _24, _25, _26, _27, _28, _29, _30, _31, _32, walk_1_aout, walk_1_bout;

  DotMatrix #(.matrixcols(32), .matrixrows(32)) dotmatrix_1 (
    .col0(_1), .col1(_2), .col2(_3), .col3(_4), .col4(_5), .col5(_6), .col6(in_7), .col7(in_8), .col8(_9),
    .col9(_10), .col10(_11), .col11(_12), .col12(_13), .col13(_14), .col14(_15), .col15(_16), .col16(_17),
    .col17(_18), .col18(_19), .col19(_20), .col20(_21), .col21(_22), .col22(_23), .col23(_24), .col24(_25),
    .col25(_26), .col26(_27), .col27(_28), .col28(_29), .col29(_30), .col30(_31), .col31(_32));
  jump jump_1 (.clock(button_1_out), .in(in_1), .out(_1));
  jump jump_2 (.clock(button_1_out), .in(walk_1_bout), .out(_5));
  jump jump_3 (.clock(button_1_out), .in(walk_1_aout), .out(_3));
  jump jump_4 (.clock(button_1_out), .in(in_2), .out(_2));
  walk walk_1 (.clock(clock_1_out), .A(in_3), .B(in_5), .Aout(walk_1_aout), .Bout(walk_1_bout));
  jump jump_5 (.clock(button_1_out), .in(in_4), .out(_4));
  Clock clock_1 (.out(clock_1_out));
  jump jump_6 (.clock(button_1_out), .in(in_6), .out(_6));
  Button button_1 (.out(button_1_out));

  assign in_9 = in_8;
  assign in_10 = in_8;
  assign in_11 = in_8;
  assign in_12 = in_8;
  assign in_13 = in_8;
  assign in_14 = in_8;
  assign in_15 = in_8;
  assign in_16 = in_8;
  assign in_17 = in_8;
  assign in_18 = in_8;
  assign in_19 = in_8;
  assign in_20 = in_8;
  assign in_21 = in_8;

  // Other names for the same wires on the sheet: _7[31:0] = in_7; _8[31:0] = in_8; vec_adr[31:0] = in_32
endmodule

module walk (
  input  clock,
  input  [31:0] A,
  input  [31:0] B,
  output [31:0] Aout,
  output [31:0] Bout
);

  wire [1:1] not_1_out, not_2_out;

  not not_1 (not_1_out[1], A[1]);
  not not_2 (not_2_out[1], B[1]);
  Multiplexer #(.width(32)) multiplexer_1 (
    .in0({B[31:2], not_2_out[1], B[0]}), .in1(B), .out(Bout), .sel(clock));  // open: en
  Multiplexer #(.width(32)) multiplexer_2 (
    .in0(A), .in1({A[31:2], not_1_out[1], A[0]}), .out(Aout), .sel(clock));  // open: en
endmodule

module jump (
  input  clock,
  input  [31:0] in,
  output [31:0] out
);

  wire [0:0] multiplexer_1_out, not_1_out;
  wire [31:0] shifter_1_out;

  not not_1 (not_1_out[0], in[0]);
  Multiplexer #(.width(32)) multiplexer_1 (
    .in0({in[31:1], not_1_out[0]}), .in1(shifter_1_out), .out({out[31:1], multiplexer_1_out[0]}), .sel(clock));  // open: en
  Shifter #(.width(32), .shift("rl")) shifter_1 (.in({in[31:1], not_1_out[0]}), .\dist (5'b00001), .out(shifter_1_out));
  not not_2 (out[0], multiplexer_1_out[0]);
endmodule
